# Fritzing sketch Final (saved by Fritzing 0.9.3b)
circuit board: 17cm x 9cm
breadboards: 2

parts:
  Main_Arduino_DUE = Arduino Due (Rev2b)
  Raspberry_Pi_3 = Raspberry Pi 3 [part_number=RPI-3-V1.2]
  7_4V_Power_Suply = Header 2 [package=screwterminal-3.5mm-2_lock]
  7_4_IN- = female pin header, 1 pin [form="♀ (female)"]
  7_4V_IN+ = female pin header, 1 pin [form="♀ (female)"]
  5V_OUT- = female pin header, 1 pin [form="♀ (female)"]
  5V_OUT+ = female pin header, 1 pin [form="♀ (female)"]
  7_4V_OUT_(Ardu) = Header 2 [package=screwterminal-3.5mm-2_lock]
  5V_OUT_(Rasp) = Header 2 [package=screwterminal-3.5mm-2_lock]
  Servo_X = Dagu DGServo 9g header (male) [package=THT]
  Servo_Y = Dagu DGServo 9g header (male) [package=THT]
  LED_1 = female pin header, 4 pins [form="♀ (female)"]
  LED_2 = female pin header, 4 pins [form="♀ (female)"]
  LED_3 = female pin header, 4 pins [form="♀ (female)"]
  LED_4_-_SHOT = female pin header, 4 pins [form="♀ (female)"]
  R1 = Resistor [tolerance=±5% resistance=220 package=THT]
  C2 = Ceramic Capacitor [capacitance=100nF package="100 mil [THT, multilayer]"]
  C3 = Ceramic Capacitor [capacitance=100nF package="100 mil [THT, multilayer]"]
  C4 = Ceramic Capacitor [capacitance=100nF package="100 mil [THT, multilayer]"]
  C1 = Ceramic Capacitor [capacitance=100nF package="100 mil [THT, multilayer]"]
  S1 = Toggle Switch [package=THT]
  J1 = female pin header, 2 pins [form="♀ (female)"]  # not connected
  OLED = female pin header, 4 pins [form="♀ (female)"]
  POLOLU_DRIVER = Generic female header - 7 pins [form="♀ (female)" package=THT]
  J3 = Generic female header - 7 pins [form="♀ (female)" package=THT]
  MOTOR_A = Header 2 [package=screwterminal-3.5mm-2_lock]
  MOTOR_B = Header 2 [package=screwterminal-3.5mm-2_lock]
  ESP = female pin header, 4 pins [form="♀ (female)"]
  ESP1 = female pin header, 4 pins [form="♀ (female)"]
  ENCODER_A = female pin header, 4 pins [form="♀ (female)"]
  ENCODER_B = female pin header, 4 pins [form="♀ (female)"]

nets:
  N1: Main_Arduino_DUE.D16/TX2, ESP1.pin1
  N2: Main_Arduino_DUE.D17/RX2, ESP.pin4
  N3: Main_Arduino_DUE.D18/TX1, Raspberry_Pi_3.GPIO15
  N4: Main_Arduino_DUE.D19/RX1, Raspberry_Pi_3.GPIO14
  N5: Main_Arduino_DUE.D20/SDA3, OLED.pin4
  N6: Main_Arduino_DUE.D21/SCL3, OLED.pin3
  N7: Main_Arduino_DUE.IOREF, LED_1.pin2, LED_2.pin2, LED_3.pin2, LED_4_-_SHOT.pin2, C2.1, C3.1, C4.1, C1.1, OLED.pin1, POLOLU_DRIVER.VCC, ESP.pin1
  VCC: Main_Arduino_DUE.5V, Servo_X.Vcc, Servo_Y.Vcc, ENCODER_A.pin1, ENCODER_B.pin1
  GND: Main_Arduino_DUE.GND, 7_4V_Power_Suply.2, 7_4_IN-.pin1, 7_4V_OUT_(Ardu).2, Servo_X.gnd, Servo_Y.gnd, LED_1.pin3, LED_2.pin3, LED_3.pin3, LED_4_-_SHOT.pin3, C2.0, C3.0, C4.0, C1.0, OLED.pin2, POLOLU_DRIVER.GND, J3.GND, ESP1.pin4, ENCODER_A.pin4, ENCODER_B.pin4
  N8: Main_Arduino_DUE.D8_PWM, Servo_X.pulse
  N9: Main_Arduino_DUE.D9_PWM, Servo_Y.pulse
  N10: Main_Arduino_DUE.D12_PWM, R1.Pin_0
  N11: Main_Arduino_DUE.D2_PWM, ESP.pin3
  N12: Main_Arduino_DUE.D3_PWM, POLOLU_DRIVER.BENBL
  N13: Main_Arduino_DUE.D4_PWM/SS1, POLOLU_DRIVER.AENBL
  N14: Main_Arduino_DUE.D22, POLOLU_DRIVER.APHASE
  N15: Main_Arduino_DUE.D23, POLOLU_DRIVER.BPHASE
  N16: Main_Arduino_DUE.D30, POLOLU_DRIVER.MODE
  N17: Main_Arduino_DUE.D40, ENCODER_A.pin2
  N18: Main_Arduino_DUE.D41, ENCODER_A.pin3
  N19: Main_Arduino_DUE.D42, ENCODER_B.pin2
  N20: Main_Arduino_DUE.D43, ENCODER_B.pin3
  N21: 7_4V_Power_Suply.1, S1.L2
  N22: 7_4V_IN+.pin1, 7_4V_OUT_(Ardu).1, S1.COM, J3.VIN
  N23: 5V_OUT-.pin1, 5V_OUT_(Rasp).2
  N24: 5V_OUT+.pin1, 5V_OUT_(Rasp).1
  N25: LED_1.pin1, LED_2.pin4
  N26: LED_1.pin4, R1.Pin_1
  N27: LED_2.pin1, LED_3.pin4
  N28: LED_3.pin1, LED_4_-_SHOT.pin4
  N29: J3.BOUT2, MOTOR_A.1
  N30: J3.BOUT1, MOTOR_A.2
  N31: J3.AOUT2, MOTOR_B.1
  N32: J3.AOUT1, MOTOR_B.2

notes:
  7.4V LiPo
  5V Raspberry
  5V Arduino
  3.3V Arduino
  Regulator Napięcia na 5V
  47/23mm
  17/8 piny
  KOLORY KABLI:
  NIEBIESKI - GND
  CZERWONY - 7.4V
  POMARAŃCZOWY - 5V
  ŻÓŁTY - 3.3V
  DOUT, 3.3V, GND, DIN
  VCC, GND, SCL, SDA
  VCC, RST, CH_PD, TX
  RX, GPIO 0, GPIO 2, GND
  5V, ENCO_1, ENCO_2, GND

custom parts:
  Generic female header - 7 pins: Generic female header
  Generic female header - 7 pins: Generic female header
